# Fritzing sketch plant-waterer (saved by Fritzing 0.9.3b)
breadboards: 1

parts:
  Part1 = Arduino Uno (Rev3)
  Water_pump = DC Motor
  Part2 = Soil Moisture Sensor
  U1 = G3VM-61E1 [package=g3vm-61e1]
  LED3 = smd LED [color="Green (560nm)" package="1206 [SMD]"]

nets:
  N1: Part1.A0, Part2.SIG
  N2: Part1.D13/SCK, LED3.anode
  GND: Part1.GND, Water_pump.pin_1, Part2.GND, U1.P$5, LED3.cathode
  N3: Part1.D3_PWM, U1.P$6
  5V: Part1.5V, Part2.VCC, U1.P$2, U1.P$3
  N4: Water_pump.pin_2, U1.P$1
